# Fritzing sketch robot seguidor de luz (saved by Fritzing 0.9.3b)
breadboards: 1

parts:
  BAT1 = BC9VPC [package=bc9vpc]
  LDR_Izquierdo = Photocell (LDR) [package=THT]
  Q1_2N2222A = NPN-Transistor [package="TO92 [THT]"]
  Q2_2N2222A = NPN-Transistor [package="TO92 [THT]"]
  Q3_2N2222 = NPN-Transistor [package="TO92 [THT]"]
  Q4_2N2222 = NPN-Transistor [package="TO92 [THT]"]
  R1 = Resistor [tolerance=±5% resistance=100k package="1206 [SMD]"]
  R1_2 = Resistor [tolerance=±5% resistance=1k package="1206 [SMD]"]
  R3 = Resistor [tolerance=±5% resistance=1k package="1206 [SMD]"]
  LDR_Derecho = Photocell (LDR) [package=THT]
  R9 = Resistor [tolerance=±5% resistance=100k package="1206 [SMD]"]
  LED1 = smd LED [color="Red (633nm)" package="1206 [SMD]"]
  LED2 = smd LED [color="Red (633nm)" package="1206 [SMD]"]
  R10 = Resistor [tolerance=±5% resistance=1k package="1206 [SMD]"]
  R11 = Resistor [tolerance=±5% resistance=1k package="1206 [SMD]"]
  M1_Motor_izquierdo = DC Motor
  M2_Motor_derecho = DC Motor

nets:
  N1: BAT1.V+, R1.Pin_1, R3.Pin_1, R9.Pin_1, R11.Pin_1, M2_Motor_derecho.pin_2
  N2: BAT1.V-, LDR_Izquierdo.pin_0, Q1_2N2222A.C, Q2_2N2222A.C, Q3_2N2222.C, Q4_2N2222.C, LDR_Derecho.pin_1
  N3: LDR_Izquierdo.pin_1, R9.Pin_0, R10.Pin_0
  N4: Q1_2N2222A.E, R3.Pin_0, LED1.cathode
  N5: Q1_2N2222A.B, R1_2.Pin_1
  N6: Q2_2N2222A.E, M1_Motor_izquierdo.pin_1
  N7: Q2_2N2222A.B, LED1.anode
  N8: Q3_2N2222.E, LED2.cathode, R11.Pin_0
  N9: Q3_2N2222.B, R10.Pin_1
  N10: Q4_2N2222.E, M2_Motor_derecho.pin_1
  N11: Q4_2N2222.B, LED2.anode
  N12: R1.Pin_0, R1_2.Pin_0, LDR_Derecho.pin_0

notes:
  El circuito del lado derecho debe controlar el motor del lado izquierdo Y el circuito del lado izquierdo debe controlar el motor derecho.
  R: Resistencia
  Q: Transistor
  M: Motor
